# Fritzing sketch potencjometrDioda (saved by Fritzing 0.9.3b)
breadboards: 1

parts:
  R1 = Rotary Potentiometer (Small) [maximum_resistance=100kΩ package=THT]
  Part1 = Arduino Uno (Rev3)
  LED1 = LED - 3mm [color="Red (635nm)" package="3 mm [THT]"]
  R2 = Resistor [tolerance=±5% resistance=1k package=THT]

nets:
  N1: R1.leg1, Part1.GND, LED1.cathode
  N2: R1.wiper, Part1.A0
  N3: R1.leg2, Part1.5V
  N4: Part1.D3_PWM, R2.Pin_1
  N5: LED1.anode, R2.Pin_0
